# Fritzing sketch FullSchema (saved by Fritzing 0.9.3b)
breadboards: 1

parts:
  Part2 = Arduino Uno (Rev3)  # not connected
  Part3 = Arduino Ethernet Shield (Rev3)
  RHT1 = Humidity and Temperature Sensor RHT03
  Part4 = Barometric Pressure Sensor - BMP085 Breakout

nets:
  N1: Part3.D2, RHT1.Data-signal
  5V: Part3.5V, RHT1.Vcc
  N2: Part3.GND, RHT1.GND_2
  N3: Part3.A4/SDA, Part4.GND
  N4: Part3.A5/SCL, Part4.VCC
